# Fritzing sketch zumo (saved by Fritzing 0.9.2b)
breadboards: 1

parts:
  R1 = Resistor [tolerance=±5% resistance=220 package=THT]
  Part1 = Arduino Uno (Rev3)
  Part2 = Arduino Uno (Rev3) - ICSP
  LED1 = smd LED [color="Red (633nm)" package="0805 [SMD]"]
  Part3 = SRF05 Ultrasonic Rangefinder
  Part4 = SRF05 Ultrasonic Rangefinder
  LED2 = smd LED [color="Yellow (585nm)" package="0805 [SMD]"]
  VCC1 = Battery block 9V

nets:
  N1: R1.Pin_0, LED1.cathode, LED2.cathode
  GND: R1.Pin_1, Part1.GND, Part2.GND, Part3.GND, Part4.GND, VCC1.-
  N2: Part1.A4/SDA, Part2.A4/SDA
  N3: Part1.A5/SCL, Part2.A5/SCL
  VCC: Part2.5V, Part3.VCC, Part4.VCC, VCC1.+
  N4: Part2.D10_PWM/SS, LED1.anode
  N5: Part2.D11_PWM/MOSI, LED2.anode
  N6: Part2.D2, Part3.Echo
  N7: Part2.D3_PWM, Part3.Trig
  N8: Part2.D6_PWM, Part4.Trig
  N9: Part2.D7, Part4.Echo
